// Logisim project memory.circ as structural Verilog: 2 circuits, main circuit main
module main (
);

  wire clock_1_out, controlled_buffer_1_out, dipswitch_2_sw1, dipswitch_2_sw2, dipswitch_2_sw3,
       dipswitch_2_sw4, dipswitch_2_sw5, dipswitch_2_sw6, dipswitch_2_sw7, dipswitch_2_sw8, dipswitch_3_sw1,
       dipswitch_3_sw2, dipswitch_3_sw3;
  wire [7:0] dipswitch_1_sw1, ram_1_data, tristatebuffer_1_o7;

  DipSwitch dipswitch_1 (
    .sw1(dipswitch_1_sw1[0]), .sw2(dipswitch_1_sw1[1]), .sw3(dipswitch_1_sw1[2]), .sw4(dipswitch_1_sw1[3]),
    .sw5(dipswitch_1_sw1[4]), .sw6(dipswitch_1_sw1[5]), .sw7(dipswitch_1_sw1[6]), .sw8(dipswitch_1_sw1[7]));
  assign controlled_buffer_1_out = dipswitch_3_sw2 ? clock_1_out : 1'bz;  // Controlled_Buffer controlled_buffer_1
  Clock clock_1 (.out(clock_1_out));
  RAM #(.bus("separate")) ram_1 (
    .addr(dipswitch_1_sw1), .din(tristatebuffer_1_o7), .data(ram_1_data), .clk(controlled_buffer_1_out));  // open: str, sel, ld, clr
  triStateBuffer tristatebuffer_1 (
    .O0(tristatebuffer_1_o7[7]), .O1(tristatebuffer_1_o7[6]), .O2(tristatebuffer_1_o7[5]),
    .O3(tristatebuffer_1_o7[4]), .O4(tristatebuffer_1_o7[3]), .O5(tristatebuffer_1_o7[2]),
    .O6(tristatebuffer_1_o7[1]), .O7(tristatebuffer_1_o7[0]), .I0(ram_1_data[7]), .I1(ram_1_data[6]),
    .I2(ram_1_data[5]), .I3(ram_1_data[4]), .I4(ram_1_data[3]), .I5(ram_1_data[2]), .I6(ram_1_data[1]),
    .I7(ram_1_data[0]), .OUT_2(dipswitch_3_sw3));  // open: OUT
  DotMatrix #(.matrixcols(8), .matrixrows(1)) dotmatrix_1 (
    .col0(tristatebuffer_1_o7[0]), .col1(tristatebuffer_1_o7[1]), .col2(tristatebuffer_1_o7[2]),
    .col3(tristatebuffer_1_o7[3]), .col4(tristatebuffer_1_o7[4]), .col5(tristatebuffer_1_o7[5]),
    .col6(tristatebuffer_1_o7[6]), .col7(tristatebuffer_1_o7[7]));
  DipSwitch dipswitch_2 (
    .sw1(dipswitch_2_sw1), .sw2(dipswitch_2_sw2), .sw3(dipswitch_2_sw3), .sw4(dipswitch_2_sw4),
    .sw5(dipswitch_2_sw5), .sw6(dipswitch_2_sw6), .sw7(dipswitch_2_sw7), .sw8(dipswitch_2_sw8));
  triStateBuffer tristatebuffer_2 (
    .O0(tristatebuffer_1_o7[0]), .O1(tristatebuffer_1_o7[1]), .O2(tristatebuffer_1_o7[2]),
    .O3(tristatebuffer_1_o7[3]), .O4(tristatebuffer_1_o7[4]), .O5(tristatebuffer_1_o7[5]),
    .O6(tristatebuffer_1_o7[6]), .O7(tristatebuffer_1_o7[7]), .I0(dipswitch_2_sw1), .I1(dipswitch_2_sw2),
    .I2(dipswitch_2_sw3), .I3(dipswitch_2_sw4), .I4(dipswitch_2_sw5), .I5(dipswitch_2_sw6),
    .I6(dipswitch_2_sw7), .I7(dipswitch_2_sw8), .OUT_2(dipswitch_3_sw1));  // open: OUT
  DipSwitch dipswitch_3 (
    .sw1(dipswitch_3_sw1), .sw2(dipswitch_3_sw2), .sw3(dipswitch_3_sw3));  // open: sw4, sw5, sw6, sw7, sw8

  // Notes on the sheet:
  //   Memory Address Register
  //   BUS IN
  //   Ram IN
  //   Ram OUT
endmodule

module triStateBuffer (
  input  I0,
  input  I1,
  input  I2,
  input  I3,
  input  I4,
  input  I5,
  input  I6,
  input  I7,
  input  OUT,
  input  OUT_2,
  output O0,
  output O1,
  output O2,
  output O3,
  output O4,
  output O5,
  output O6,
  output O7
);

  assign O0 = OUT ? I0 : 1'bz;  // Controlled_Buffer controlled_buffer_1
  assign O1 = OUT ? I1 : 1'bz;  // Controlled_Buffer controlled_buffer_2
  assign O3 = OUT ? I3 : 1'bz;  // Controlled_Buffer controlled_buffer_3
  assign O2 = OUT ? I2 : 1'bz;  // Controlled_Buffer controlled_buffer_4
  assign O4 = OUT ? I4 : 1'bz;  // Controlled_Buffer controlled_buffer_5
  assign O5 = OUT ? I5 : 1'bz;  // Controlled_Buffer controlled_buffer_6
  assign O6 = OUT ? I6 : 1'bz;  // Controlled_Buffer controlled_buffer_7
  assign O7 = OUT ? I7 : 1'bz;  // Controlled_Buffer controlled_buffer_8

  assign OUT_2 = OUT;
endmodule
